// Logisim project RegisterTransfer4.circ as structural Verilog: 3 circuits, main circuit main
module main (
  input  I2,
  input  I1,
  input  I0,
  output [31:0] R3,
  output [31:0] R4,
  output [31:0] R1,
  output [31:0] R2
);

  wire clock_1_out, decoder32_1_r1, decoder32_1_r2, decoder32_1_r3, decoder32_1_r4;
  wire [31:0] mux_1_out_7;

  DECODER32 decoder32_1 (
    .I2(I2), .I0(I0), .R1(decoder32_1_r1), .R2(decoder32_1_r2), .R3(decoder32_1_r3), .R4(decoder32_1_r4));
  MUX mux_1 (.R1(R1), .R2(R2), .R3(R3), .R4(R4), .I2(I2), .I1(I1), .out_7(mux_1_out_7));
  Register #(.width(32)) u_R1 (.D(mux_1_out_7), .en(decoder32_1_r1), .Q(R1), .clk(clock_1_out));  // open: clr
  Register #(.width(32)) u_R2 (.D(mux_1_out_7), .en(decoder32_1_r2), .Q(R2), .clk(clock_1_out));  // open: clr
  Clock clock_1 (.out(clock_1_out));
  Register #(.width(32)) u_R3 (.D(mux_1_out_7), .en(decoder32_1_r3), .Q(R3), .clk(clock_1_out));  // open: clr
  Register #(.width(32)) u_R4 (.D(mux_1_out_7), .en(decoder32_1_r4), .Q(R4), .clk(clock_1_out));  // open: clr
endmodule

module MUX (
  input  [31:0] R1,
  input  [31:0] R2,
  input  [31:0] R3,
  input  [31:0] R4,
  input  I2,
  input  I1,
  output [31:0] out_7
);

  wire [31:0] and_1_out, and_2_out, and_3_out, and_4_out, bit_extender_1_out, bit_extender_2_out, not_1_out,
       not_2_out;

  assign bit_extender_1_out = {{31{I2}}, I2};  // Bit_Extender bit_extender_1
  assign not_1_out = ~bit_extender_2_out;  // NOT_Gate not_1, 32 bits wide
  assign not_2_out = ~bit_extender_1_out;  // NOT_Gate not_2, 32 bits wide
  assign bit_extender_2_out = {{31{I1}}, I1};  // Bit_Extender bit_extender_2
  assign and_1_out = R1 & not_2_out & not_1_out;  // AND_Gate and_1, 32 bits wide
  assign and_2_out = R2 & not_2_out & bit_extender_2_out;  // AND_Gate and_2, 32 bits wide
  assign and_3_out = R3 & bit_extender_1_out & not_1_out;  // AND_Gate and_3, 32 bits wide
  assign and_4_out = R4 & bit_extender_1_out & bit_extender_2_out;  // AND_Gate and_4, 32 bits wide
  assign out_7 = and_1_out | and_2_out | and_3_out | and_4_out;  // OR_Gate or_1, 32 bits wide
endmodule

module DECODER32 (
  input  I2,
  input  I0,
  output R1,
  output R2,
  output R3,
  output R4
);

  wire not_1_out, not_2_out;

  not not_1 (not_1_out, I2);
  not not_2 (not_2_out, I0);
  and and_1 (R1, I2, not_2_out);
  and and_2 (R2, I2, I0);
  and and_3 (R3, not_1_out, not_2_out);
  and and_4 (R4, not_1_out, I0);
endmodule
